# Fritzing sketch mAteo (saved by Fritzing 0.9.2b)
circuit board: 8.46667cm x 5.64444cm
breadboards: 1

parts:
  S1 = Pushbutton [package="[THT]"]
  S2 = Pushbutton [package="[THT]"]
  S3 = Pushbutton [package="[THT]"]
  S4 = Pushbutton [package="[THT]"]
  S5 = Pushbutton [package="[THT]"]
  R1 = Resistor [tolerance=±5% resistance=220 package=THT]
  R2 = Resistor [tolerance=±5% resistance=1k package=THT]
  R3 = Resistor [tolerance=±5% resistance=4.7 package=THT]
  R4 = Resistor [tolerance=±5% resistance=10k package=THT]
  R5 = Resistor [tolerance=±5% resistance=10k package=THT]
  Part1 = Arduino Nano (Rev3.0)
  Squix1 = OLED 0.96" 128x64 I2C SSD1306
  Part2 = Adafruit BMP180
  DHT1 = DHT22 Humidity and Temperature Sensor

nets:
  N1: S1.Pin_1, S1.Pin_2, S2.Pin_1, S2.Pin_2, S3.Pin_1, S3.Pin_2, S4.Pin_1, S4.Pin_2, S5.Pin_1, S5.Pin_2, R5.Pin_1, Part1.A6
  5V: S1.Pin_3, S1.Pin_4, R1.Pin_1, R2.Pin_0, R3.Pin_0, R4.Pin_0, Part1.5V, Squix1.VCC, Part2.+5V, DHT1.VDD
  N2: S2.Pin_3, S2.Pin_4, R1.Pin_0
  N3: S3.Pin_3, S3.Pin_4, R2.Pin_1
  N4: S4.Pin_3, S4.Pin_4, R3.Pin_1
  N5: S5.Pin_3, S5.Pin_4, R4.Pin_1
  GND: R5.Pin_0, Part1.GND, Squix1.GND, Part2.GND, DHT1.GND
  N6: Part1.D2, Part1.D3
  N7: Part1.D12/MISO, DHT1.DATA
  N8: Part1.A5, Squix1.SCA, Part2.SDA
  N9: Part1.A4, Squix1.SCL, Part2.SCL

custom parts:
  Adafruit BMP180: This precision sensor from Bosch is the best low-cost sensing solution for measuring barometric pressure and temperature. Because pressure changes with altitude you can also use it as an altimeter! The sensor is soldered onto a PCB with a 3.3V regulator, I2C level shifter and pull-up resistors on the I2C pins. The BMP180 is the next-generation of sensors from Bosch, and replaces the BMP085.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
